// Logisim project PROJETO.circ as structural Verilog
module main (
  input  [3:0] in_1,
  input  [3:0] in_2,
  output [3:0] out_3
);

  wire somadorcompleto_1_cout, somadorcompleto_2_cout, somadorcompleto_3_cout, somadorcompleto_4_cout;

  somadorCompleto somadorcompleto_1 (
    .Cout(somadorcompleto_1_cout), .B(in_1[3]), .Cin(somadorcompleto_2_cout), .A(in_2[3]), .S(out_3[3]));
  somadorCompleto somadorcompleto_2 (
    .Cout(somadorcompleto_2_cout), .B(in_1[2]), .Cin(somadorcompleto_3_cout), .A(in_2[2]), .S(out_3[2]));
  somadorCompleto somadorcompleto_3 (
    .Cout(somadorcompleto_3_cout), .B(in_1[1]), .Cin(somadorcompleto_4_cout), .A(in_2[1]), .S(out_3[1]));
  Hex_Digit_Display hex_digit_display_1 (.value(out_3));  // open: dp
  somadorCompleto somadorcompleto_4 (.Cout(somadorcompleto_4_cout), .B(in_1[0]), .Cin(1'b0), .A(in_2[0]), .S(out_3[0]));
  // also tied to GND on the sheet: somadorcompleto_1_cout
endmodule

module meioSomador (
  input  A,
  input  B,
  output S,
  output Cout
);

  xor xor_1 (S, A, B);
  and and_1 (Cout, A, B);
endmodule

module somadorCompleto (
  input  A,
  input  B,
  input  Cin,
  output S,
  output Cout
);

  wire meiosomador_1_cout, meiosomador_1_s, meiosomador_2_cout;

  meioSomador meiosomador_1 (.Cout(meiosomador_1_cout), .B(B), .S(meiosomador_1_s), .A(A));
  meioSomador meiosomador_2 (.Cout(meiosomador_2_cout), .B(Cin), .S(S), .A(meiosomador_1_s));
  or or_1 (Cout, meiosomador_2_cout, meiosomador_1_cout);
endmodule

module multiplicador (
  input  [7:0] in_1,
  input  [7:0] in_2,
  output [7:0] out_3
);

  Multiplier multiplier_1 (.a(in_1), .b(in_2), .out(out_3));  // open: cin, cout
endmodule

module somador8bits (
  input  [7:0] in_1,
  input  [7:0] in_2,
  output [7:0] out_3
);

  wire somadorcompleto_1_cout, somadorcompleto_2_cout, somadorcompleto_3_cout, somadorcompleto_4_cout,
       somadorcompleto_5_cout, somadorcompleto_6_cout, somadorcompleto_7_cout, somadorcompleto_8_cout;

  somadorCompleto somadorcompleto_1 (
    .Cout(somadorcompleto_1_cout), .B(in_1[7]), .Cin(somadorcompleto_2_cout), .A(in_2[7]), .S(out_3[7]));
  somadorCompleto somadorcompleto_2 (
    .Cout(somadorcompleto_2_cout), .B(in_1[6]), .Cin(somadorcompleto_3_cout), .A(in_2[6]), .S(out_3[6]));
  somadorCompleto somadorcompleto_3 (
    .Cout(somadorcompleto_3_cout), .B(in_1[5]), .Cin(somadorcompleto_4_cout), .A(in_2[5]), .S(out_3[5]));
  somadorCompleto somadorcompleto_4 (
    .Cout(somadorcompleto_4_cout), .B(in_1[4]), .Cin(somadorcompleto_5_cout), .A(in_2[4]), .S(out_3[4]));
  somadorCompleto somadorcompleto_5 (
    .Cout(somadorcompleto_5_cout), .B(in_1[3]), .Cin(somadorcompleto_6_cout), .A(in_2[3]), .S(out_3[3]));
  somadorCompleto somadorcompleto_6 (
    .Cout(somadorcompleto_6_cout), .B(in_1[2]), .Cin(somadorcompleto_7_cout), .A(in_2[2]), .S(out_3[2]));
  somadorCompleto somadorcompleto_7 (
    .Cout(somadorcompleto_7_cout), .B(in_1[1]), .Cin(somadorcompleto_8_cout), .A(in_2[1]), .S(out_3[1]));
  somadorCompleto somadorcompleto_8 (.Cout(somadorcompleto_8_cout), .B(in_1[0]), .Cin(1'b0), .A(in_2[0]), .S(out_3[0]));
  // also tied to GND on the sheet: somadorcompleto_1_cout
endmodule

module meioSubtrator (
  input  in_1,
  input  in_2,
  output out_3,
  output out_4
);

  xor xor_1 (out_3, in_1, in_2);
  and and_1 (out_4, in_2, ~in_1);  // AND_Gate
endmodule

module subtratorCompleto (
  input  A,
  input  B,
  input  Cin,
  output S,
  output Cout
);

  wire meiosubtrator_1_out_3, meiosubtrator_1_out_4, meiosubtrator_2_out_4;

  meioSubtrator meiosubtrator_1 (.out_4(meiosubtrator_1_out_4), .out_3(meiosubtrator_1_out_3), .in_2(B), .in_1(A));
  meioSubtrator meiosubtrator_2 (.out_4(meiosubtrator_2_out_4), .out_3(S), .in_2(Cin), .in_1(meiosubtrator_1_out_3));
  or or_1 (Cout, meiosubtrator_2_out_4, meiosubtrator_1_out_4);
endmodule

module subtrator8bits (
  input  [7:0] in_1,
  input  [7:0] in_2,
  output [7:0] out_3
);

  wire subtratorcompleto_1_cout, subtratorcompleto_2_cout, subtratorcompleto_3_cout,
       subtratorcompleto_4_cout, subtratorcompleto_5_cout, subtratorcompleto_6_cout,
       subtratorcompleto_7_cout, subtratorcompleto_8_cout;

  subtratorCompleto subtratorcompleto_1 (
    .Cout(subtratorcompleto_1_cout), .S(out_3[7]), .Cin(subtratorcompleto_2_cout), .B(in_1[7]), .A(in_2[7]));
  subtratorCompleto subtratorcompleto_2 (
    .Cout(subtratorcompleto_2_cout), .S(out_3[6]), .Cin(subtratorcompleto_3_cout), .B(in_1[6]), .A(in_2[6]));
  subtratorCompleto subtratorcompleto_3 (
    .Cout(subtratorcompleto_3_cout), .S(out_3[5]), .Cin(subtratorcompleto_4_cout), .B(in_1[5]), .A(in_2[5]));
  subtratorCompleto subtratorcompleto_4 (
    .Cout(subtratorcompleto_4_cout), .S(out_3[4]), .Cin(subtratorcompleto_5_cout), .B(in_1[4]), .A(in_2[4]));
  subtratorCompleto subtratorcompleto_5 (
    .Cout(subtratorcompleto_5_cout), .S(out_3[3]), .Cin(subtratorcompleto_6_cout), .B(in_1[3]), .A(in_2[3]));
  subtratorCompleto subtratorcompleto_6 (
    .Cout(subtratorcompleto_6_cout), .S(out_3[2]), .Cin(subtratorcompleto_7_cout), .B(in_1[2]), .A(in_2[2]));
  subtratorCompleto subtratorcompleto_7 (
    .Cout(subtratorcompleto_7_cout), .S(out_3[1]), .Cin(subtratorcompleto_8_cout), .B(in_1[1]), .A(in_2[1]));
  subtratorCompleto subtratorcompleto_8 (
    .Cout(subtratorcompleto_8_cout), .S(out_3[0]), .Cin(1'b0), .B(in_1[0]), .A(in_2[0]));
  // also tied to GND on the sheet: subtratorcompleto_1_cout
endmodule

module deslocadorDireita (
  input  [7:0] in_1,
  input  [2:0] in_2,
  output [7:0] out_3
);

  Shifter #(.shift("lr")) shifter_1 (.in(in_1), .\dist (in_2), .out(out_3));
endmodule

module deslocadorEsquerda (
  input  [7:0] in_1,
  input  [2:0] in_2,
  output [7:0] out_3
);

  Shifter shifter_1 (.in(in_1), .\dist (in_2), .out(out_3));
endmodule

module or8bits (
  input  [7:0] in_1,
  input  [7:0] in_2,
  output [7:0] out_3
);

  assign out_3 = in_1 | in_2;  // OR_Gate or_1, 8 bits wide
endmodule

module and8bits (
  input  [7:0] in_1,
  input  [7:0] in_2,
  output [7:0] out_3
);

  assign out_3 = in_1 & in_2;  // AND_Gate and_1, 8 bits wide
endmodule

module xor8bits (
  input  [7:0] in_1,
  input  [7:0] in_2,
  output [7:0] out_3
);

  assign out_3 = in_1 ^ in_2;  // XOR_Gate xor_1, 8 bits wide
endmodule

module nand8bits (
  input  [7:0] in_1,
  input  [7:0] in_2,
  output [7:0] out_3
);

  assign out_3 = ~(in_1 & in_2);  // NAND_Gate nand_1, 8 bits wide
endmodule

module not8bits (
  input  [7:0] in_1,
  output [7:0] out_2
);

  assign out_2 = ~in_1;  // NOT_Gate not_1, 8 bits wide
endmodule

module xnor8bits (
  input  [7:0] in_1,
  input  [7:0] in_2,
  output [7:0] out_3
);

  assign out_3 = ~(in_1 ^ in_2);  // XNOR_Gate xnor_1, 8 bits wide
endmodule

module nor8bits (
  input  [7:0] A,
  input  [7:0] B,
  output [7:0] S
);

  assign S = ~(A | B);  // NOR_Gate nor_1, 8 bits wide
endmodule
