// Logisim project ProjetoULA_Bernardo_Campos_328_Natacha_Calixto_243.circ as structural Verilog: 1 circuit, main circuit ula
module ula (
  input  [7:0] A,
  input  [7:0] B,
  input  [2:0] Cin0,
  input  [3:0] OPCODE,
  input  [2:0] Cin1,
  output [7:0] S
);

  wire [7:0] and8bits_1_out_3, demultiplexer_1_out10, deslocadordireita_1_out_3, deslocadoresquerda_1_out_3,
       multiplicador_1_out_3, nand8bits_1_out_3, nor8bits_1_s, not8bits_1_out_2, or8bits_1_out_3,
       somador8bits_1_out_3, subtrator8bits_1_out_3, xnor8bits_1_out_3, xor8bits_1_out_3;
  wire [15:0] demultiplexer_1_out0, demultiplexer_1_out1, demultiplexer_1_out2, demultiplexer_1_out4,
       demultiplexer_1_out5, demultiplexer_1_out7, demultiplexer_1_out8, demultiplexer_1_out9,
       demultiplexer_1_out11, demultiplexer_1_out12, demultiplexer_1_out14, demultiplexer_1_out15;

  Demultiplexer #(.select(4), .width(16), .enable("false")) demultiplexer_1 (
    .out0(demultiplexer_1_out0), .out1(demultiplexer_1_out1), .out2(demultiplexer_1_out2),
    .out3(demultiplexer_1_out0), .out4(demultiplexer_1_out4), .out5(demultiplexer_1_out5),
    .out6(demultiplexer_1_out0), .out7(demultiplexer_1_out7), .out8(demultiplexer_1_out8),
    .out9(demultiplexer_1_out9), .out10({demultiplexer_1_out5[15:8], demultiplexer_1_out10}),
    .out11(demultiplexer_1_out11), .out12(demultiplexer_1_out12), .out13(demultiplexer_1_out0),
    .out14(demultiplexer_1_out14), .out15(demultiplexer_1_out15), .in({B, A}), .sel(OPCODE));
  nor8bits nor8bits_1 (.A(demultiplexer_1_out1[7:0]), .B(demultiplexer_1_out1[15:8]), .S(nor8bits_1_s));
  not8bits not8bits_1 (.in_1(demultiplexer_1_out2[7:0]), .out_2(not8bits_1_out_2));
  nand8bits nand8bits_1 (
    .in_1(demultiplexer_1_out4[7:0]), .in_2(demultiplexer_1_out4[15:8]), .out_3(nand8bits_1_out_3));
  deslocadorDireita deslocadordireita_1 (
    .in_1(demultiplexer_1_out5[7:0]), .in_2(Cin0), .out_3(deslocadordireita_1_out_3));
  xor8bits xor8bits_1 (.in_1(demultiplexer_1_out7[7:0]), .in_2(demultiplexer_1_out7[15:8]), .out_3(xor8bits_1_out_3));
  multiplicador multiplicador_1 (
    .in_1(demultiplexer_1_out8[7:0]), .in_2(demultiplexer_1_out8[15:8]), .out_3(multiplicador_1_out_3));
  and8bits and8bits_1 (.in_1(demultiplexer_1_out9[7:0]), .in_2(demultiplexer_1_out9[15:8]), .out_3(and8bits_1_out_3));
  xnor8bits xnor8bits_1 (
    .in_1(demultiplexer_1_out11[7:0]), .in_2(demultiplexer_1_out11[15:8]), .out_3(xnor8bits_1_out_3));
  somador8bits somador8bits_1 (
    .in_1(demultiplexer_1_out12[7:0]), .in_2(demultiplexer_1_out12[15:8]), .out_3(somador8bits_1_out_3));
  or8bits or8bits_1 (.in_1(demultiplexer_1_out14[7:0]), .in_2(demultiplexer_1_out14[15:8]), .out_3(or8bits_1_out_3));
  subtrator8bits subtrator8bits_1 (
    .in_1(demultiplexer_1_out15[7:0]), .in_2(demultiplexer_1_out15[15:8]), .out_3(subtrator8bits_1_out_3));
  deslocadorEsquerda deslocadoresquerda_1 (
    .in_1(demultiplexer_1_out10), .in_2(Cin1), .out_3(deslocadoresquerda_1_out_3));
  Multiplexer #(.select(4), .width(8), .enable("false")) multiplexer_1 (
    .in0(demultiplexer_1_out2[15:8]), .in1(nor8bits_1_s), .in2(not8bits_1_out_2), .in4(nand8bits_1_out_3),
    .in5(deslocadordireita_1_out_3), .in6(demultiplexer_1_out2[15:8]), .in7(xor8bits_1_out_3),
    .in8(multiplicador_1_out_3), .in9(and8bits_1_out_3), .in10(deslocadoresquerda_1_out_3),
    .in11(xnor8bits_1_out_3), .in12(somador8bits_1_out_3), .in13(demultiplexer_1_out2[15:8]),
    .in14(or8bits_1_out_3), .in15(subtrator8bits_1_out_3), .out(S), .sel(OPCODE));  // open: in3
  // also tied to GND on the sheet: {demultiplexer_1_out0[0], demultiplexer_1_out0[1], demultiplexer_1_out0[2], demultiplexer_1_out0[3], demultiplexer_1_out0[4], demultiplexer_1_out0[5], demultiplexer_1_out0[6], demultiplexer_1_out0[7], demultiplexer_1_out0[8], demultiplexer_1_out0[9], demultiplexer_1_out0[10], demultiplexer_1_out0[11], demultiplexer_1_out0[12], demultiplexer_1_out0[13], demultiplexer_1_out0[14], demultiplexer_1_out0[15], demultiplexer_1_out2[8], demultiplexer_1_out2[9], demultiplexer_1_out2[10], demultiplexer_1_out2[11], demultiplexer_1_out2[12], demultiplexer_1_out2[13], demultiplexer_1_out2[14], demultiplexer_1_out2[15], demultiplexer_1_out5[8], demultiplexer_1_out5[9], demultiplexer_1_out5[10], demultiplexer_1_out5[11], demultiplexer_1_out5[12], demultiplexer_1_out5[13], demultiplexer_1_out5[14], demultiplexer_1_out5[15]}

  // Notes on the sheet:
  //   Projeto ALU
endmodule
